# Fritzing sketch sketch_droplet (saved by Fritzing 0.7.1b)
breadboards: 1

parts:
  Arduino1 = Arduino
  R1 = Resistor [tolerance=±5% resistance=1k package=THT]
  M1 = DC Motor
  Q1 = NPN-Transistor [package="TO92 [THT]"]
  U1 = Optocoupler [package=THT]
  R2 = Resistor [tolerance=±5% resistance=220 package=THT]
  Power_plug1 = Power plug
  M2 = DC Motor
  M3 = DC Motor
  Q2 = NPN-Transistor [package="TO92 [THT]"]
  Q3 = NPN-Transistor [package="TO92 [THT]"]
  R3 = Resistor [tolerance=±5% resistance=1k package=THT]
  R4 = Resistor [tolerance=±5% resistance=1k package=THT]
  U2 = Optocoupler [package=THT]
  R5 = Resistor [tolerance=±5% resistance=220 package=THT]

nets:
  GND: Arduino1.GND, Q1.C, U1.Pin_2, Power_plug1.GND, Q2.C, Q3.C, U2.Pin_2
  N1: Arduino1.D12, Arduino1.D10, R1.Pin_0, R4.Pin_0
  N2: Arduino1.D11, R3.Pin_0
  N3: Arduino1.D9, R2.Pin_0
  N4: Arduino1.D8, R5.Pin_0
  N5: R1.Pin_1, Q1.E
  N6: M1.pin_1, Power_plug1.VCC, M2.pin_1, M3.pin_1
  N7: M1.pin_2, Q1.B
  N8: U1.Pin_1, R2.Pin_1
  N9: U1.Pin_4, U2.Pin_4
  N10: M2.pin_2, Q2.B
  N11: M3.pin_2, Q3.B
  N12: Q2.E, R3.Pin_1
  N13: Q3.E, R4.Pin_1
  N14: U2.Pin_1, R5.Pin_1

notes:
  Magnetventil 12V
  12V
  EOS 7D
  Weiss: Basis
  Rot: Release
  Blau: Focus
